# Fritzing sketch Schematic (saved by Fritzing 0.9.3b)
breadboards: 2

parts:
  Squix1 = OLED 0.96" 128x64 I2C SSD1306
  Part1 = Arduino Nano (Rev3.0)
  Raspberry_Pi_Zero1 = Raspberry Pi Zero
  R1 = Resistor [tolerance=±5% resistance=470 package=THT]
  R2 = Resistor [tolerance=±5% resistance=220 package=THT]
  LED1 = RGB LED (com. cathode, rgb) [package="5 mm [THT]"]
  R3 = Resistor [tolerance=±5% resistance=470 package=THT]
  R4 = Resistor [tolerance=±5% resistance=470 package=THT]
  R5 = Resistor [tolerance=±5% resistance=470 package=THT]
  R6 = Resistor [tolerance=±5% resistance=470 package=THT]
  R7 = Resistor [tolerance=±5% resistance=470 package=THT]
  R8 = Resistor [tolerance=±5% resistance=470 package=THT]
  LED2 = RGB LED (com. cathode, rgb) [package="5 mm [THT]"]

nets:
  VCC: Squix1.VCC, Part1.5V
  GND: Squix1.GND, Part1.D0/RX, Part1.GND, Raspberry_Pi_Zero1.GPIO4, Raspberry_Pi_Zero1.GND, Raspberry_Pi_Zero1.GPIO14, R1.Pin_0, LED1.common_cathode, LED2.common_cathode
  N1: Squix1.SCL, Part1.A5
  N2: Squix1.SCA, Part1.A4
  N3: Part1.D1/TX, R2.Pin_1
  N4: Part1.D3, R3.Pin_0
  N5: Part1.D5, R4.Pin_0
  N6: Part1.D6, R5.Pin_0
  N7: Part1.D9, R6.Pin_0
  N8: Part1.D10, R7.Pin_0
  N9: Part1.D11/MOSI, R8.Pin_0
  N10: Raspberry_Pi_Zero1.GPIO17, Raspberry_Pi_Zero1.GPIO15, R1.Pin_1, R2.Pin_0
  N11: LED1.red_anode, R3.Pin_1
  N12: LED1.green_anode, R4.Pin_1
  N13: LED1.blue_anode, R5.Pin_1
  N14: R6.Pin_1, LED2.red_anode
  N15: R7.Pin_1, LED2.green_anode
  N16: R8.Pin_1, LED2.blue_anode
