# Fritzing sketch Connected_to_RaspberryPiZero (saved by Fritzing 0.9.3b)
breadboards: 1

parts:
  Part1 = Arduino Nano (Rev3.0)
  Raspberry_Pi_Zero1 = Raspberry Pi Zero
  R1 = Resistor [tolerance=±5% resistance=220 package=THT]
  R2 = Resistor [tolerance=±5% resistance=470 package=THT]

nets:
  N1: Part1.D1/TX, R2.Pin_0
  N2: Part1.D0/RX, Raspberry_Pi_Zero1.GPIO14
  GND: Part1.GND, Raspberry_Pi_Zero1.GND, R1.Pin_1
  5V: Part1.5V, Raspberry_Pi_Zero1.5V
  N3: Raspberry_Pi_Zero1.GPIO15, R1.Pin_0, R2.Pin_1
