# Fritzing sketch Output_test_schematic (saved by Fritzing 0.9.3b)
breadboards: 1

parts:
  Squix1 = OLED 0.96" 128x64 I2C SSD1306
  Part1 = Arduino Nano (Rev3.0)
  Raspberry_Pi_Zero1 = Raspberry Pi Zero
  R1 = Resistor [tolerance=±5% resistance=470 package=THT]
  R2 = Resistor [tolerance=±5% resistance=220 package=THT]
  U1 = Sharp PC817 [package=THT]
  R3 = Resistor [tolerance=±5% resistance=330 package=THT]
  R4 = Resistor [tolerance=±5% resistance=2.2k package=THT]
  IC1 = Voltage Regulator [package=to-220-alt]
  R5 = Resistor [tolerance=±5% resistance=1k package=THT]
  LED1 = LED - 5mm [color="Red (633nm)" package="5 mm [THT]"]

nets:
  VCC: Squix1.VCC, Part1.5V
  GND: Squix1.GND, Part1.D0/RX, Part1.GND, Raspberry_Pi_Zero1.GPIO4, Raspberry_Pi_Zero1.GND, Raspberry_Pi_Zero1.GPIO14, R1.Pin_0, U1.Pin_2
  N1: Squix1.SCL, Part1.A5
  N2: Squix1.SCA, Part1.A4
  N3: Part1.D1/TX, R2.Pin_1
  N4: Part1.D11/MOSI, R3.Pin_0
  N5: Raspberry_Pi_Zero1.GPIO17, Raspberry_Pi_Zero1.GPIO15, R1.Pin_1, R2.Pin_0
  N6: U1.Pin_1, R3.Pin_1
  N7: U1.Pin_4, R4.Pin_1
  N8: U1.Pin_3, IC1.GND, R5.Pin_0
  N9: R4.Pin_0, LED1.cathode
  N10: IC1.IN, LED1.anode
  N11: IC1.OUT, R5.Pin_1
